// Logisim project medium.circ as structural Verilog: 19 circuits, main circuit 1m
module _1m (
  input  in_1,
  input  in_2
);

  wire xnor_1_out;

  xnor xnor_1 (xnor_1_out, in_1, in_2);
  LED led_1 (.in(xnor_1_out));
endmodule

module _2m (
  input  in_1,
  input  in_2
);

  wire or_1_out;

  or or_1 (or_1_out, in_1, in_2);
  LED led_1 (.in(or_1_out));
endmodule

module _3m (
  input  in_1,
  input  in_2
);

  wire xor_1_out;

  xor xor_1 (xor_1_out, in_1, in_2);
  LED led_1 (.in(xor_1_out));
endmodule

module _4m (
  input  in_1,
  input  in_2
);

  wire xor_1_out;

  xor xor_1 (xor_1_out, in_1, in_2);
  LED led_1 (.in(xor_1_out));
endmodule

module _5m (
  input  in_1,
  input  in_2
);

  wire xor_1_out;

  xor xor_1 (xor_1_out, in_1, in_2);
  LED led_1 (.in(xor_1_out));
endmodule

module _6m (
  input  in_1,
  input  in_2
);

  wire and_1_out;

  and and_1 (and_1_out, ~in_1, ~in_2);  // AND_Gate
  LED led_1 (.in(and_1_out));
endmodule

module _7m (
  input  in_1,
  input  in_2
);

  wire and_1_out;

  and and_1 (and_1_out, in_1, in_2);
  LED led_1 (.in(and_1_out));
endmodule

module _8m (
  input  in_1
);

  wire not_1_out, xor_1_out;

  not not_1 (not_1_out, in_1);
  xor xor_1 (xor_1_out, not_1_out, in_1);
  LED led_1 (.in(xor_1_out));
endmodule

module _9m (
  input  in_1
);

  wire nor_1_out;

  nor nor_1 (nor_1_out, in_1, in_1);
  LED led_1 (.in(nor_1_out));
endmodule

module _10m (
  input  in_1
);

  wire and_1_out;

  and and_1 (and_1_out, in_1, in_1);
  LED led_1 (.in(and_1_out));
endmodule

module _11m (
  input  in_1,
  input  in_2
);

  wire and_1_out;

  and and_1 (and_1_out, in_1, in_2);
  LED led_1 (.in(and_1_out));
endmodule

module _12m (
  input  in_1,
  input  in_2
);

  wire or_1_out;

  or or_1 (or_1_out, in_1, in_2);
  LED led_1 (.in(or_1_out));
endmodule

module _13m (
  input  in_1,
  input  in_2
);

  wire or_1_out;

  or or_1 (or_1_out, ~in_1, ~in_2);  // OR_Gate
  LED led_1 (.in(or_1_out));
endmodule

module _14m (
  input  in_1,
  input  in_2
);

  wire xnor_1_out;

  xnor xnor_1 (xnor_1_out, in_1, in_2);
  LED led_1 (.in(xnor_1_out));
endmodule

module _15m (
  input  in_1,
  input  in_2
);

  wire or_1_out;

  or or_1 (or_1_out, in_1, in_2);
  LED led_1 (.in(or_1_out));
endmodule

module _16m (
  input  in_1,
  input  in_2
);

  wire xnor_1_out;

  xnor xnor_1 (xnor_1_out, in_1, in_2);
  LED led_1 (.in(xnor_1_out));
endmodule

module _17m (
  input  in_1,
  input  in_2
);

  wire or_1_out;

  or or_1 (or_1_out, ~in_1, ~in_2);  // OR_Gate
  LED led_1 (.in(or_1_out));
endmodule

module _18m (
  input  in_1,
  input  in_2
);

  wire xnor_1_out;

  xnor xnor_1 (xnor_1_out, in_1, in_2);
  LED led_1 (.in(xnor_1_out));
endmodule

module _19m (
  input  in_1,
  input  in_2
);

  wire and_1_out;

  and and_1 (and_1_out, in_1, in_2);
  LED led_1 (.in(and_1_out));
endmodule
